// Logisim project alu.circ as structural Verilog: 1 circuit, main circuit alu
module alu (
  input  [31:0] A,
  input  [31:0] B,
  input  [3:0] ALUSel,
  output [31:0] ALUResult
);

  wire [0:0] slt2;
  wire [31:0] add0, and7, mul8, mulh9, mulhu11, multiplexer_1_out, multiplexer_2_out, multiplexer_3_out,
       multiplexer_4_out, multiplexer_5_out, multiplexer_6_out, multiplexer_7_out, multiplexer_8_out,
       multiplexer_9_out, multiplexer_10_out, multiplexer_11_out, multiplexer_12_out, multiplexer_13_out,
       multiplexer_14_out, multiplier_1_cout, six_or, sll1, sra13, srl5, sub12, undriven, xor4;

  Adder #(.width(32)) adder_1 (.a(A), .b(B), .out(add0));  // open: cin, cout
  Shifter #(.width(32)) shifter_1 (.in(A), .\dist (B[4:0]), .out(sll1));
  Comparator #(.width(32)) comparator_1 (.a(A), .b(B), .lt(slt2[0]));  // open: gt, eq
  assign xor4 = A ^ B;  // XOR_Gate xor_1, 32 bits wide
  Shifter #(.shift("lr"), .width(32)) shifter_2 (.in(A), .\dist (B[4:0]), .out(srl5));
  assign six_or = A | B;  // OR_Gate or_1, 32 bits wide
  assign and7 = A & B;  // AND_Gate and_1, 32 bits wide
  Multiplier #(.width(32)) multiplier_1 (.a(A), .b(B), .out(mul8), .cout(multiplier_1_cout));  // open: cin
  Multiplier #(.width(32)) multiplier_2 (.a(A), .b(B), .out(mulh9), .cin(multiplier_1_cout));  // open: cout
  Multiplier #(.width(32)) multiplier_3 (.a(A), .b(B), .out(mulhu11), .cin(multiplier_1_cout));  // open: cout
  Subtractor #(.width(32)) subtractor_1 (.a(A), .b(B), .out(sub12));  // open: bin, bout
  Shifter #(.shift("lr"), .width(32)) shifter_3 (.in(A), .\dist (B[4:0]), .out(sra13));
  // Probe on add0
  // Probe on sll1
  // Probe on {{31{1'b0}}, slt2[0]}
  // Probe on xor4
  // Probe on srl5
  // Probe on six_or
  // Probe on and7
  // Probe on mul8
  // Probe on mulh9
  // Probe on mulhu11
  // Probe on sub12
  // Probe on sra13
  // Probe on undriven
  // Probe on B
  Multiplexer #(.width(32)) multiplexer_1 (.in0(add0), .in1(sll1), .out(multiplexer_1_out), .sel(ALUSel[0]));
  Multiplexer #(.width(32)) multiplexer_2 (
    .in0({{31{1'b0}}, slt2[0]}), .out(multiplexer_2_out), .sel(ALUSel[0]));  // open: in1
  Multiplexer #(.width(32)) multiplexer_3 (.in0(xor4), .in1(srl5), .out(multiplexer_3_out), .sel(ALUSel[0]));
  Multiplexer #(.width(32)) multiplexer_4 (.in0(six_or), .in1(and7), .out(multiplexer_4_out), .sel(ALUSel[0]));
  Multiplexer #(.width(32)) multiplexer_5 (.in0(mul8), .in1(mulh9), .out(multiplexer_5_out), .sel(ALUSel[0]));
  Multiplexer #(.width(32)) multiplexer_6 (.in1(mulhu11), .out(multiplexer_6_out), .sel(ALUSel[0]));  // open: in0
  Multiplexer #(.width(32)) multiplexer_7 (.in0(sub12), .in1(sra13), .out(multiplexer_7_out), .sel(ALUSel[0]));
  Multiplexer #(.width(32)) multiplexer_8 (.in1(B), .out(multiplexer_8_out), .sel(ALUSel[0]));  // open: in0
  Multiplexer #(.width(32)) multiplexer_9 (
    .in0(multiplexer_1_out), .in1(multiplexer_2_out), .out(multiplexer_9_out), .sel(ALUSel[1]));
  Multiplexer #(.width(32)) multiplexer_10 (
    .in0(multiplexer_3_out), .in1(multiplexer_4_out), .out(multiplexer_10_out), .sel(ALUSel[1]));
  Multiplexer #(.width(32)) multiplexer_11 (
    .in0(multiplexer_5_out), .in1(multiplexer_6_out), .out(multiplexer_11_out), .sel(ALUSel[1]));
  Multiplexer #(.width(32)) multiplexer_12 (
    .in0(multiplexer_7_out), .in1(multiplexer_8_out), .out(multiplexer_12_out), .sel(ALUSel[1]));
  Multiplexer #(.width(32)) multiplexer_13 (
    .in0(multiplexer_9_out), .in1(multiplexer_10_out), .out(multiplexer_13_out), .sel(ALUSel[2]));
  Multiplexer #(.width(32)) multiplexer_14 (
    .in0(multiplexer_11_out), .in1(multiplexer_12_out), .out(multiplexer_14_out), .sel(ALUSel[2]));
  Multiplexer #(.width(32)) multiplexer_15 (
    .in0(multiplexer_13_out), .in1(multiplexer_14_out), .out(ALUResult), .sel(ALUSel[3]));

  // Other names for the same wires on the sheet: bsel15[31:0] = B

  // Notes on the sheet:
  //   INPUTS to your circuit
  //   DON'T CHANGE THE LOCATIONS OF THE INPUTS AND OUTPUTS!
  //   OUTPUT from your circuit
endmodule
