// Logisim project control-logic.circ as structural Verilog: 1 circuit, main circuit control_logic
module control_logic (
  input  [31:0] Instruction,
  input  BrEq,
  input  BrLt,
  output PCSel,
  output RegWEn,
  output [2:0] ImmSel,
  output BrUn,
  output ASel,
  output BSel,
  output [3:0] ALUSel,
  output MemWEn,
  output [1:0] WBSel
);

  wire B, comparator_10_eq, comparator_11_eq, comparator_12_eq, I, I_0, I_1, J, R, S, U_0, U_1;
  wire [5:0] controlled_buffer_1_out, controlled_buffer_3_out, ROM_input;
  wire [15:14] rom_1_data;

  Comparator #(.width(7)) comparator_1 (.a(7'b0110011), .b(Instruction[6:0]), .eq(R));  // open: gt, lt
  Comparator #(.width(7)) comparator_2 (.a(7'b0000011), .b(Instruction[6:0]), .eq(I_0));  // open: gt, lt
  Comparator #(.width(7)) comparator_3 (.a(7'b0010011), .b(Instruction[6:0]), .eq(I_1));  // open: gt, lt
  Comparator #(.width(7)) comparator_4 (.a(7'b0100011), .b(Instruction[6:0]), .eq(S));  // open: gt, lt
  Comparator #(.width(7)) comparator_5 (.a(7'b1100011), .b(Instruction[6:0]), .eq(B));  // open: gt, lt
  Comparator #(.width(7)) comparator_6 (.a(7'b0010111), .b(Instruction[6:0]), .eq(U_0));  // open: gt, lt
  Comparator #(.width(7)) comparator_7 (.a(7'b0110111), .b(Instruction[6:0]), .eq(U_1));  // open: gt, lt
  Comparator #(.width(7)) comparator_8 (.a(7'b1101111), .b(Instruction[6:0]), .eq(J));  // open: gt, lt
  Comparator #(.width(7)) comparator_9 (.a(7'b1100111), .b(Instruction[6:0]), .eq(I));  // open: gt, lt
  ROM #(.addrWidth(6), .dataWidth(16)) rom_1 (
    .addr(ROM_input), .data({rom_1_data, WBSel, MemWEn, ALUSel, BSel, ASel, BrUn, ImmSel, RegWEn}));
  Comparator #(.width(3)) comparator_10 (.a(3'b000), .b(Instruction[14:12]), .eq(comparator_10_eq));  // open: gt, lt
  Comparator #(.width(3)) comparator_11 (.a(3'b000), .b(Instruction[14:12]), .eq(comparator_11_eq));  // open: gt, lt
  Comparator #(.width(7)) comparator_12 (.a({7{1'b0}}), .b(Instruction[31:25]), .eq(comparator_12_eq));  // open: gt, lt
  assign controlled_buffer_1_out = comparator_10_eq ? {6{1'b0}} : 6'bz;  // Controlled_Buffer controlled_buffer_1
  assign ROM_input = R ? controlled_buffer_1_out : 6'bz;  // Controlled_Buffer controlled_buffer_2
  assign controlled_buffer_3_out = comparator_11_eq ? 6'b001111 : 6'bz;  // Controlled_Buffer controlled_buffer_3
  assign ROM_input = I ? controlled_buffer_3_out : 6'bz;  // Controlled_Buffer controlled_buffer_4

  // Other names for the same wires on the sheet: opcode[6:0] = Instruction[6:0]; funct3[2:0] = Instruction[14:12];
  //   funct7[6:0] = Instruction[31:25]

  // Notes on the sheet:
  //   INPUTS to your circuit
  //   Connect ROM Input here ->
  //   rd
  //   rs1
  //   rs2
  //   imm
  //   contents of rom_1 (hex, n*v repeats v):
  //   15*0 1041
  //   https://docs.google.com/spreadsheets/d/1vts9_fcR0R5lcWhoOKzbi-m19LdhPlSol3BM-b1i-8Q/edit#gid=1550641118
  //   https://docs.google.com/spreadsheets/d/19MkohNO2yCCk6rRMd5Y-KDsqoHkXe3wCx7QYsCBHFKQ/view#gid=0
  //   ROM FOR CONTROL LOGIC
  //   DON'T CHANGE THE LOCATIONS OF THE INPUTS AND OUTPUTS!
  //   This is only if you choose to do the ROM option
  //   OUTPUT from your circuit
  //   Reminder: If using ROM, use combinational logic for PCSel
endmodule
