// Logisim project cpu.circ as structural Verilog: 1 circuit, main circuit cpu
module cpu (
  input  clk,
  input  [31:0] Instruction,
  input  [31:0] MemReadData,
  output [31:0] MemAddress,
  output [31:0] ProgramCounter,
  output [31:0] ra,
  output [31:0] sp,
  output [31:0] t0,
  output [31:0] t1,
  output [31:0] t2,
  output [31:0] s0,
  output [31:0] s1,
  output [31:0] a0,
  output [3:0] MemWriteMask,
  output [31:0] MemWriteData
);

  wire partial_store_1_p1, partial_store_1_p2, partial_store_1_p4, partial_store_1_p6, regfile_1_p3,
       regfile_1_p4, regfile_1_p6, regfile_1_p16, regfile_1_p18, RegWEn;
  wire [3:0] AluSel;
  wire [31:0] A, adder_1_out, B;

  Register #(.width(32)) PC (.D(adder_1_out), .clk(clk), .Q(ProgramCounter));  // open: en, clr
  Adder #(.width(32)) adder_1 (.a(ProgramCounter), .b(32'h4), .out(adder_1_out));  // open: cin, cout
  control_logic control_logic_1 (
    .Instruction(Instruction), .RegWEn(RegWEn), .ALUSel(AluSel));  // open: BrEq, BrLt, PCSel, ImmSel, BrUn, ASel, BSel, MemWEn, WBSel
  // regfile regfile_1: pin names not known; wires that end beside it: RegWEn, clk, regfile_1_p3, regfile_1_p4, regfile_1_p4, regfile_1_p6, ra, sp, t0, t1, t2, s0, s1, a0, regfile_1_p6, regfile_1_p16, regfile_1_p16, regfile_1_p18, regfile_1_p18
  imm_gen imm_gen_1 (.Instruction(Instruction), .Immediate(B));  // open: ImmSel
  alu alu_1 (.A(A), .B(B), .ALUSel(AluSel));  // open: ALUResult
  // branch_comp branch_comp_1: pin names not known
  // partial_store partial_store_1: pin names not known; wires that end beside it: partial_store_1_p1, partial_store_1_p2, partial_store_1_p2, partial_store_1_p4, partial_store_1_p4, partial_store_1_p6, partial_store_1_p1, partial_store_1_p6
  // partial_load partial_load_1: pin names not known

  // Notes on the sheet:
  //   To IMEM
  //   IMEM (do **NOT** move this)
  //   From IMEM
  //   Inputs/Outputs for testing. Do **NOT** move these.
  //   It is OK to move the PC, RegFile, ALU, MEM, Branch Comp, Imm Gen, Partial Load, Partial Store and Control Logic to wherever is most convenient for you when constructing your CPU, and to delete this text
  //   here's from imm gen
  //   To DMEM
  //   DMEM (do **NOT** move this)
  //   From DMEM
endmodule
