// Logisim project imm-gen.circ as structural Verilog: 1 circuit, main circuit imm_gen
module imm_gen (
  input  [31:0] Instruction,
  input  [2:0] ImmSel,
  output [31:0] Immediate
);


  assign Immediate = {{20{1'b0}}, Instruction[31:20]};

  // Notes on the sheet:
  //   INPUTS to your circuit
  //   6:0 opcode
  //   11:7 rd
  //   14:12 funct3
  //   19:15 rs1
  //   31:20 immidiate[11:0]
  //   DON'T CHANGE THE LOCATIONS OF THE INPUTS AND OUTPUTS!
  //   OUTPUT from your circuit
endmodule
